# Fritzing sketch Trafic_Lamp (saved by Fritzing 0.9.3b)
breadboards: 1

parts:
  Part1 = Arduino Uno (Rev3)
  LED1 = LED - 5mm [color="Red (633nm)" package="5 mm [THT]"]
  LED2 = LED - 5mm [color="Green (555nm)" package="5 mm [THT]"]
  R1 = Resistor [tolerance=±5% resistance=220 package=THT]
  R2 = Resistor [tolerance=±5% resistance=220 package=THT]
  LED3 = LED - 5mm [color="Red (633nm)" package="5 mm [THT]"]
  LED4 = LED - 5mm [color="Yellow (595nm)" package="5 mm [THT]"]
  LED5 = LED - 5mm [color="Green (555nm)" package="5 mm [THT]"]
  R3 = Resistor [tolerance=±5% resistance=220 package=THT]
  R4 = Resistor [tolerance=±5% resistance=220 package=THT]
  R5 = Resistor [tolerance=±5% resistance=220 package=THT]
  S1 = Pushbutton [package="[THT]"]

nets:
  N1: Part1.D8, R4.Pin_1
  N2: Part1.D10_PWM/SS, R5.Pin_1
  N3: Part1.D11_PWM/MOSI, R1.Pin_1
  N4: Part1.D12/MISO, R2.Pin_1
  N5: Part1.D3_PWM, S1.Pin_3, S1.Pin_4
  N6: Part1.D6_PWM, R3.Pin_1
  N7: Part1.GND, LED1.cathode, LED2.cathode, LED3.cathode, LED4.cathode, LED5.cathode, S1.Pin_1, S1.Pin_2
  N8: LED1.anode, R2.Pin_0
  N9: LED2.anode, R1.Pin_0
  N10: LED3.anode, R5.Pin_0
  N11: LED4.anode, R4.Pin_0
  N12: LED5.anode, R3.Pin_0

// code stored in the sketch: trafic_lamp.ino
const int buttonPin = 3;
const int yayakirmizled = 13; 
const int yayayesilled = 11; 
const int aracyesilled = 6; 
const int aracsariled = 8; 
const int arackirmizled = 10; 
bool toggleState = false;
unsigned long simdizaman;
unsigned long oncezaman=0;
int zaman = 0;

void setup()
{
   pinMode(buttonPin, INPUT_PULLUP);
   pinMode(aracyesilled, OUTPUT);
   pinMode(aracsariled, OUTPUT);
   pinMode(arackirmizled, OUTPUT);
   pinMode(yayakirmizled, OUTPUT);
   pinMode(yayayesilled, OUTPUT);
   Serial.begin(9600);
   digitalWrite(aracyesilled,HIGH);
   digitalWrite(yayakirmizled,HIGH);
  
}

void loop()
{

  simdizaman = millis(); 

  if(simdizaman-oncezaman > 1000){
    zaman++;
    oncezaman = simdizaman;
  }
     
 int readButton = digitalRead(buttonPin);
  
  if (readButton == 0) {
    
    toggleState = ! toggleState;
        
    if (zaman > 30){

     digitalWrite(aracyesilled,LOW);
     delay(500);
     digitalWrite(aracyesilled,HIGH); 
     delay(1000);
     digitalWrite(aracyesilled,LOW);
     delay(500);
     digitalWrite(aracyesilled,HIGH); 
     delay(1000); 
     digitalWrite(aracyesilled,LOW);
     delay(500);
     digitalWrite(aracyesilled,HIGH); 
     delay(1000);        
     digitalWrite(aracyesilled,LOW);       
     delay(1000);             
     digitalWrite(aracsariled,HIGH);  
     delay(3000);           
     digitalWrite(aracsariled,LOW);  
     digitalWrite(arackirmizled,HIGH);
     digitalWrite(yayayesilled,HIGH); 
     digitalWrite(yayakirmizled,LOW); 
     delay(15000);       
  
     digitalWrite(yayayesilled,LOW); 
      delay(500);
     digitalWrite(yayayesilled,HIGH); 
      delay(500);
     digitalWrite(yayayesilled,LOW); 
      delay(500);
     digitalWrite(yayayesilled,HIGH); 
      delay(500);
     digitalWrite(yayayesilled,LOW); 
      delay(500);
     digitalWrite(yayayesilled,HIGH); 
            delay(500);
    digitalWrite(yayayesilled,LOW); 
         delay(1000);
    digitalWrite(yayakirmizled,HIGH);    
       delay(5000);
             
     digitalWrite(aracsariled,HIGH);  
      delay(2000);
             
     digitalWrite(aracsariled,LOW);  
     digitalWrite(arackirmizled,LOW);  
     digitalWrite(aracyesilled,HIGH);  
      
     zaman = 0;
      
    }else if(zaman < 30){
      int KalanSn = 30 - zaman;
      delay(KalanSn*1000);
         digitalWrite(aracyesilled,LOW);
      delay(500);
     digitalWrite(aracyesilled,HIGH); 
     delay(1000);
     digitalWrite(aracyesilled,LOW);
     delay(500);
     digitalWrite(aracyesilled,HIGH); 
     delay(1000); 
     digitalWrite(aracyesilled,LOW);
     delay(500);
     digitalWrite(aracyesilled,HIGH); 
     delay(1000);      
     digitalWrite(aracyesilled,LOW);       
     delay(1000);           
     digitalWrite(aracsariled,HIGH);  
     delay(3000);         
     digitalWrite(aracsariled,LOW);  
     digitalWrite(arackirmizled,HIGH);
     digitalWrite(yayayesilled,HIGH); 
     digitalWrite(yayakirmizled,LOW); 
     delay(15000);   
 
    digitalWrite(yayayesilled,LOW); 
      delay(500);
    digitalWrite(yayayesilled,HIGH); 
      delay(500);
    digitalWrite(yayayesilled,LOW); 
      delay(500);
    digitalWrite(yayayesilled,HIGH); 
      delay(500);
    digitalWrite(yayayesilled,LOW); 
      delay(500);
    digitalWrite(yayayesilled,HIGH); 
      delay(500);
    digitalWrite(yayayesilled,LOW); 
      delay(1000);
    digitalWrite(yayakirmizled,HIGH);    
      delay(5000);
    digitalWrite(aracsariled,HIGH);  
      delay(2000);
             
     digitalWrite(aracsariled,LOW);  
     digitalWrite(arackirmizled,LOW);  
     digitalWrite(aracyesilled,HIGH);   
     zaman = 0;
    }
    delay(500);
  }
  
}
